# Fritzing sketch Fritzing-ProjectIOT-GR09 (saved by Fritzing 1.0.6)
breadboards: 1

parts:
  R1 = Resistor [tolerance=±5% power=0.25W resistance=220 package=THT]
  A1 = DHT22 module
  A2 = PIR sensor (non-bendable legs)
  J2 = Piezo Speaker
  R2 = Photocell (LDR) [power=0.25W dark_resistance_@0.01lx=300kΩ light_resistance_@100lx=400Ω luminance=10lx package=THT]
  LED1 = RGB LED (com. anode, rbg) [color="Red (633nm)" current=0.030A package="5 mm [THT]"]
  esp1 = ESP32 DevKitc V4
  R3 = Resistor [tolerance=±5% power=0.25W resistance=220 package=THT]
  R4 = Resistor [tolerance=±5% power=0.25W resistance=220 package=THT]
  R5 = Resistor [tolerance=±5% power=0.25W resistance=220 package=THT]
  J3 = Basic Servo

nets:
  N1: R1.Pin_0, esp1.IO14
  N2: R1.Pin_1, LED1.red_cathode
  VDD: A1.+, A2.VDD, R2.pin_1, LED1.common_anode, esp1.3V3, J3.vcc
  N3: A1.-, J2.pin1, esp1.GND#32, R3.Pin_0, J3.gnd
  N4: A2.SIG, esp1.IO27
  N5: A2.GND, esp1.GND#18
  N6: J2.pin2, esp1.IO26
  N7: R2.pin_0, esp1.IO34, R3.Pin_1
  N8: LED1.blue_cathode, R4.Pin_0
  N9: LED1.green_cathode, R5.Pin_0
  N10: esp1.IO25, J3.pulse
  N11: esp1.IO12, R5.Pin_1
  N12: esp1.IO13, R4.Pin_1

custom parts:
  DHT22 module: DHT22 module. Pins VCC Data GND.
  PIR sensor (non-bendable legs): Generic PIR sensor
  ESP32 DevKitc V4: ESP32-DevKitC board with ESP32-WROOM-32 module. ESP32-DevKitC V4 is a small-sized ESP32-based development board produced by Espressif. Most of the pins on the ESP module are broken out to the pin headers on the board. The pins D0, D1, D2, D3, CMD and CLK are used internally for communication between ESP32 and SPI flash memory. They are grouped on both sides near the USB connector. Avoid using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
